# Fritzing sketch ampel (saved by Fritzing 0.9.9b)
breadboards: 1

parts:
  Mod1 = Raspberry Pi 4B
  LED1 = LED - 5mm [color="Red (633nm)" current=0.030 package="5 mm [THT]"]
  LED2 = LED - 5mm [color="Yellow (585nm)" current=0.030 package="5 mm [THT]"]
  LED3 = LED - 5mm [color="Green (560nm)" current=0.030 package="5 mm [THT]"]
  LED4 = LED - 5mm [color="Red (633nm)" current=0.030 package="5 mm [THT]"]
  LED5 = LED - 5mm [color="Green (560nm)" current=0.030 package="5 mm [THT]"]
  R1 = Resistor [tolerance=±5% power=0.25 resistance=220 package=THT]
  R2 = Resistor [tolerance=±5% power=0.25 resistance=220 package=THT]
  R3 = Resistor [tolerance=±5% power=0.25 resistance=220 package=THT]
  R4 = Resistor [tolerance=±5% power=0.25 resistance=220 package=THT]
  R5 = Resistor [tolerance=±5% power=0.25 resistance=220 package=THT]
  R6 = Resistor [tolerance=±5% power=0.25 resistance=1k package=THT]
  R7 = Resistor [tolerance=±5% power=0.25 resistance=10k package=THT]
  S1 = Pushbutton [package="[THT]"]

nets:
  N1: Mod1.3V3, R7.Pin_0
  N2: Mod1.GPIO8, R6.Pin_1
  N3: Mod1.GPIO5, R1.Pin_1
  N4: Mod1.GPIO6, R2.Pin_1
  N5: Mod1.GPIO13, R3.Pin_1
  N6: Mod1.GND, LED1.cathode, LED2.cathode, LED3.cathode, LED4.cathode, LED5.cathode, S1.Pin_3, S1.Pin_4
  N7: Mod1.GPIO19, R4.Pin_1
  N8: Mod1.GPIO26, R5.Pin_1
  N9: LED1.anode, R1.Pin_0
  N10: LED2.anode, R2.Pin_0
  N11: LED3.anode, R3.Pin_0
  N12: LED4.anode, R4.Pin_0
  N13: LED5.anode, R5.Pin_0
  N14: R6.Pin_0, R7.Pin_1, S1.Pin_1, S1.Pin_2
